# Fritzing sketch dual_Garage_Controller (saved by Fritzing 0.9.4)
breadboards: 1

parts:
  WeMos_D1_Mini1 = WeMos D1 Mini
  Part1 = Adafruit BME680
  S1 = SWITCH-MOMENTARY-2 [package=reed_switch_plastic]
  S2 = SWITCH-MOMENTARY-2 [package=reed_switch_plastic]
  WeMos_D1_Mini_Relay_Shield_V1 = WeMos D1 Mini Relay Shield V2
  WeMos_D1_Mini_Relay_Shield_V2 = WeMos D1 Mini Relay Shield V2

nets:
  5V: WeMos_D1_Mini1.5V, Part1.VIN, WeMos_D1_Mini_Relay_Shield_V1.5V, WeMos_D1_Mini_Relay_Shield_V2.5V
  N1: WeMos_D1_Mini1.D0, S2.1
  N2: WeMos_D1_Mini1.D1, Part1.SCK/SCL
  N3: WeMos_D1_Mini1.D2, Part1.SDI/SDA
  N4: WeMos_D1_Mini1.D5, S1.2
  N5: WeMos_D1_Mini1.D6, WeMos_D1_Mini_Relay_Shield_V1.D1
  N6: WeMos_D1_Mini1.D7, WeMos_D1_Mini_Relay_Shield_V2.D1
  N7: WeMos_D1_Mini1.G, Part1.GND, S1.1, S2.2, WeMos_D1_Mini_Relay_Shield_V2.G
